# Fritzing sketch ESP8266 to CAN (saved by Fritzing 0.9.3b)

parts:
  Board1 = MCP2515_CAN board [part_number=4081 package="DIP (Dual Inline) [THT]"]
  Part1 = Logic Level Converter
  Part2 = Logic Level Converter
  Gizwits_WiFi_Witty_ESP-12F1 = Gizwits WiFi Witty ESP-12F

nets:
  N1: Board1.connector0, Part1.TX_HV
  N2: Board1.connector1, Part1.RX_HV
  N3: Board1.connector2, Part1.RX2_HV
  N4: Board1.connector3, Part1.TX2_HV
  N5: Board1.connector4, Part2.TX_HV
  GND: Board1.connector5, Part1.GND, Part2.GND, Gizwits_WiFi_Witty_ESP-12F1.GND
  N6: Board1.connector9, Board1.connector10
  N7: Part1.TX2_LV, Gizwits_WiFi_Witty_ESP-12F1.GPIO12
  N8: Part1.RX2_LV, Gizwits_WiFi_Witty_ESP-12F1.GPIO13
  N9: Part1.RX_LV, Gizwits_WiFi_Witty_ESP-12F1.GPIO14
  N10: Part1.TX_LV, Gizwits_WiFi_Witty_ESP-12F1.GPIO4
  N11: Part2.TX_LV, Gizwits_WiFi_Witty_ESP-12F1.GPIO5

notes:
  Showing 2x4-channel level shifters. Actually used an 8-channel level shifter, but there is no part in Fritzing.
  GPIO05 is used as the CS pin. Using GPIO15 (the hardware CS pin) causes problems when booting
  +3V3
  +5V

custom parts:
  MCP2515_CAN board: MCP2525 SPI to CAN-Bus board.
