# Fritzing sketch ESP8266 to Nano to CAN (saved by Fritzing 0.9.3b)

parts:
  Board1 = MCP2515_CAN board [part_number=4081 package="DIP (Dual Inline) [THT]"]
  Part1 = Logic Level Converter
  Gizwits_WiFi_Witty_ESP-12F1 = Gizwits WiFi Witty ESP-12F
  Part3 = Arduino Nano (Rev3.0) (ICSP)
  JP1 = Header 3 [package=screwterminal-3.5mm-3_lock.007s]

nets:
  N1: Board1.connector0, Part3.D2
  N2: Board1.connector1, Part3.D13/SCK
  N3: Board1.connector2, Part3.D11/MOSI
  N4: Board1.connector3, Part3.D12/MISO
  N5: Board1.connector4, Part3.D10
  GND: Board1.connector5, Part1.GND, Gizwits_WiFi_Witty_ESP-12F1.GND, JP1.2
  N6: Board1.connector6, Part1.HV, Part3.VIN, JP1.3
  N7: Board1.connector9, Board1.connector10
  N8: Part1.LV, Gizwits_WiFi_Witty_ESP-12F1.VCC, JP1.1
  N9: Part1.RX_LV, Gizwits_WiFi_Witty_ESP-12F1.RXD
  N10: Part1.TX_LV, Gizwits_WiFi_Witty_ESP-12F1.TXD
  N11: Part1.TX_HV, Part3.D0/RX
  N12: Part1.RX_HV, Part3.D1/TX

notes:
  +3V GND +5V
  CAN Cabling (to another MCP2515 board)
  Sketch: ESP8266_WiFiTelnetToSerial
  Sketch: Nano_CANASCII_to_CAN

custom parts:
  MCP2515_CAN board: MCP2525 SPI to CAN-Bus board.
